# Fritzing sketch AlarDuino (saved by Fritzing 0.9.0b)
circuit board: 6.88566cm x 5.36311cm
breadboards: 1

parts:
  ADXL = ADXL335 Accelerometer Breakout
  TMP = TMP36 Temperature Sensor [package="TO92 [THT]"]
  JCK1 = Audio Jack (TRS) 3.5mm [package="4Ucon 08780 [THT]"]
  JCK2 = Audio Jack (TRS) 3.5mm [package="4Ucon 08780 [THT]"]
  NPN = NPN-Transistor [package="TO92 [THT]"]
  1k = Resistor [tolerance=±5% resistance=1k package=THT]
  LED = LED - 5mm [color="Red (633nm)" package="5 mm [THT]"]
  1k_2 = Resistor [tolerance=±5% resistance=1k package=THT]
  J8 = rounded female pin header, 10 pins [form="♀ (female rounded)"]
  J9 = rounded female pin header, 8 pins [form="♀ (female rounded)"]  # not connected
  J10 = rounded female pin header, 8 pins [form="♀ (female rounded)"]
  J11 = rounded female pin header, 6 pins [form="♀ (female rounded)"]
  BAT = Battery
  10nF = Ceramic Capacitor [capacitance=10nF package="100 mil [THT, multilayer]"]
  BRL = Power plug
  10uF = Electrolytic Capacitor [capacitance=10µF package="100 mil [THT, electrolytic]"]
  TMP_2 = Breadboard Trimpot
  ACC = Breadboard Trimpot
  D1 = Diode [package=diode-1n4001]
  BUZ = Buzzer 12mm [package=buzzer-12mm-ns-kit]
  RST = Pushbutton [package="[THT]"]
  J12 = rounded female pin header, 2 pins [form="♀ (female rounded)"]

nets:
  5V: ADXL.Vin, TMP.+Vs, JCK2.Tip, J10.pin5, 10uF.+, TMP_2.PIN1, ACC.PIN1
  GND/GND2: ADXL.GND, TMP.GND, JCK2.Sleeve, NPN.E, LED.cathode, J8.pin4, J10.pin6, BAT.-, 10nF.1, BRL.GND, 10uF.-, TMP_2.PIN3, ACC.PIN3, BUZ.2, RST.Pin_3
  N1: ADXL.Xout, J11.pin5
  N2: ADXL.Yout, J11.pin4
  N3: ADXL.Zout, J11.pin3
  N4: TMP.Vout, J11.pin1, 10nF.0
  N5: JCK1.Sleeve, NPN.C
  N6: JCK1.Ring, JCK1.Tip, BRL.VCC, D1.C, J12.pin1
  N7: JCK2.Ring, J8.pin6
  N8: NPN.B, 1k.Pin_1
  N9: 1k.Pin_0, J8.pin8
  N10: LED.anode, 1k_2.Pin_0
  N11: 1k_2.Pin_1, J8.pin9
  N12: J8.pin7, BUZ.1
  N13: J10.pin3, RST.Pin_1, RST.Pin_2
  N14: J10.pin8, J12.pin2
  N15: J11.pin2, TMP_2.PIN2
  N16: J11.pin6, ACC.PIN2
  N17: BAT.+, D1.A

notes:
  PIR
  SRN
  4
  ALARDUINO
  by PAKOZM
  GND
  5V
  5:APOT
  ~5
  VCC
  2016 v0.3
  ~11
  SIREN
  TMP
  0:TMP
  2:X0
  3:Y0
  4:Z0
  13
  12
  RX<-0
  TX->1
  ~3
  ~6
  ~10
  ~9
  7
  AREF
  12:PIR
  10:SRN
  9:LED
  11:BUZ
  Sound Bomb1 - Twin Piezo elements
  110dB sound output
  Only 85mA current consumption
  Compact ABS enclosure in white
  Twin wall fixing lugs
  15cm flying lead ( Black & Red)
  12VDC Powered
  http://www.w9xt.com/page_microdesign_pt7_transistor_switching.html
  hFE = 35 (worst case)
  Is = 85 (siren current)
  Ib = 85/35 = 2.5 => 3mA room
  VBE(sat) = 1V
  VP0 = 5V
  VP0 = VR1 + VBE
  VR1 = VP0 - VBE = 5 - 1 = 4V
  R = VR1/Ib = 4/0.003 = 1333
  12V
  2
  8
  A1
  1:TPOT
  AlarDuino, Car Alarm Arduino Shield, 0.3
  RST
  max=18
  max=8C
  Vin
  3.3V
  Vcc
  SCL
  SDA

custom parts:
  ADXL335 Accelerometer Breakout: ADXL335 Accelerometer Breakout board
