# Fritzing sketch EcoDuino (saved by Fritzing 0.9.0b)
circuit board: 6.88566cm x 5.36311cm
breadboards: 1

parts:
  J11 = rounded female pin header, 8 pins [form="♀ (female rounded)"]
  J12 = rounded female pin header, 6 pins [form="♀ (female rounded)"]
  J13 = rounded female pin header, 8 pins [form="♀ (female rounded)"]
  ATMEGA328P = atmega328 [package=dip]
  C1 = Electrolytic Capacitor [capacitance=10µF package="100 mil [THT, electrolytic]"]
  BAT = Battery
  XTAL = Crystal [frequency="16 Mhz" package=THT]
  C3_22_pF = Capacitor [package=cap-pth-small2]
  C4_22pF = Capacitor [package=cap-pth-small2]
  R1 = Resistor [tolerance=±5% resistance=1k package=THT]
  RST1 = Pushbutton [package="[THT]"]
  LED1 = LED - 5mm [color="Red (633nm)" package="5 mm [THT]"]
  R2 = Resistor [tolerance=±5% resistance=220 package=THT]
  IC = Voltage Regulator [package=to220-igo]
  C5 = Electrolytic Capacitor [capacitance=10µF package="100 mil [THT, electrolytic]"]
  S = Toggle Switch [package=THT]
  D1 = Diode [package=diode-1n4001]
  Power = Power plug
  J10 = rounded female pin header, 10 pins [form="♀ (female rounded)"]
  J14 = male pin header, 6 pins [form="♂ (male)"]
  C6 = Ceramic Capacitor [capacitance=0.1µF package="100 mil [THT, multilayer]"]

nets:
  D7: J11.pin1, ATMEGA328P.D7
  D6: J11.pin2, ATMEGA328P.D6_(PWM)
  D5: J11.pin3, ATMEGA328P.D5_(PWM)
  D4: J11.pin4, ATMEGA328P.D4
  D3: J11.pin5, ATMEGA328P.D3_(PWM)
  D2: J11.pin6, ATMEGA328P.D2
  D1: J11.pin7, ATMEGA328P.D1_(TX), J14.pin2
  D0: J11.pin8, ATMEGA328P.D0_(RX), J14.pin3
  A0: J12.pin1, ATMEGA328P.A0
  A1: J12.pin2, ATMEGA328P.A1
  A2: J12.pin3, ATMEGA328P.A2
  A3: J12.pin4, ATMEGA328P.A3
  A4: J12.pin5, ATMEGA328P.A4
  A5: J12.pin6, ATMEGA328P.A5
  5V/AVCC/VCC: J13.pin5, ATMEGA328P.VCC, ATMEGA328P.AVCC, C1.+, R1.Pin_0, S.COM, J14.pin4
  GND: J13.pin6, J13.pin7, ATMEGA328P.GND, C1.-, BAT.-, C3_22_pF.1, C4_22pF.2, RST1.Pin_1, RST1.Pin_2, LED1.cathode, IC.GND, C5.-, Power.GND, J10.pin4, J14.pin6
  N1: ATMEGA328P.RESET, R1.Pin_1, RST1.Pin_3, RST1.Pin_4, C6.0
  N2: ATMEGA328P.XLAT1, XTAL.pin_0, C4_22pF.1
  N3: ATMEGA328P.XLAT2, XTAL.pin_1, C3_22_pF.2
  D8: ATMEGA328P.D8, J10.pin10
  D9: ATMEGA328P.D9_(PWM), J10.pin9
  D10: ATMEGA328P.D10_(PWM), J10.pin8
  D11: ATMEGA328P.D11_(PWM), J10.pin7
  D12: ATMEGA328P.D12, J10.pin6
  D13: ATMEGA328P.D13, R2.Pin_1, J10.pin5
  AEREF pin: ATMEGA328P.AREF, J10.pin3
  N4: BAT.+, D1.A, Power.VCC
  N5: LED1.anode, R2.Pin_0
  N6: IC.IN, C5.+, D1.C
  N7: IC.OUT, S.L2
  USB 5V: S.L1
  N8: J14.pin1, C6.1

notes:
  2016 v0.1
  by PAKOZM
  ALARDUINO
  ECODUINO
  5V
  GND
  AREF
  7
  8
  ~9
  ~10
  ~6
  ~5
  4
  ~3
  2
  TX->1
  RX<-0
  ~11
  12
  13
  A4
  A3
  A2
  A0
  A1
  A5
  Vcc
  place USB at bottom
  EcoDuino, Arduino with switchable voltage regulator., 0.1
  UART
  gnd
  3v
  5v
  rx
  tx
  rst
