# Fritzing sketch RXShield (saved by Fritzing 0.9.0b)
circuit board: 4.84252cm x 5.31073cm
breadboards: 1

parts:
  PROGRAM = Pushbutton [package="[THT]"]
  RESET = Pushbutton [package="[THT]"]
  RX = female pin header, 4 pins [form="♀ (female)"]
  Attiny85 = attiny85 [package=dip]
  10K = Resistor [tolerance=±5% resistance=10k package=THT]
  47K = Resistor [tolerance=±5% resistance=47k package=THT]
  22K = Resistor [tolerance=±5% resistance=22k package=THT]
  LED1 = LED - 5mm [color="Red (633nm)" package="5 mm [THT]"]
  1K = Resistor [tolerance=±5% resistance=1k package=THT]
  J14 = rounded female pin header, 10 pins [form="♀ (female rounded)"]
  J15 = rounded female pin header, 8 pins [form="♀ (female rounded)"]
  J16 = rounded female pin header, 6 pins [form="♀ (female rounded)"]  # not connected
  J17 = rounded female pin header, 8 pins [form="♀ (female rounded)"]
  100nF = Ceramic Capacitor [capacitance=100nF package="100 mil [THT, multilayer]"]
  100nF_2 = Ceramic Capacitor [capacitance=100nF package="100 mil [THT, multilayer]"]
  J19 = rounded female pin header, 6 pins [form="♀ (female rounded)"]
  NPN = NPN-Transistor [package="TO92 [THT]"]
  22k = Resistor [tolerance=±5% resistance=22k package=THT]

nets:
  N1: PROGRAM.Pin_1, PROGRAM.Pin_2, J15.pin5
  GND/GND2: PROGRAM.Pin_3, PROGRAM.Pin_4, RESET.Pin_3, RESET.Pin_4, Attiny85.Pin_4, 47K.Pin_0, LED1.cathode, J14.pin4, J17.pin6, 100nF.0, NPN.E
  RESET: RESET.Pin_1, RESET.Pin_2, Attiny85.Pin_1, J17.pin3, J19.pin6
  N2: RX.pin1, 100nF_2.0, NPN.C
  N3: RX.pin3, 10K.Pin_1
  5V: RX.pin4, J17.pin5, 100nF_2.1
  N4: Attiny85.Pin_2, J19.pin5, 22k.Pin_1
  N5: Attiny85.Pin_3, 1K.Pin_1, J19.pin4
  N6: Attiny85.Pin_5, 47K.Pin_1, 22K.Pin_1, J19.pin3
  N7: Attiny85.Pin_6, J14.pin10, J19.pin2
  N8: Attiny85.Pin_7, 10K.Pin_0, J19.pin1
  VOUT: Attiny85.Pin_8, J17.pin4, 100nF.1
  N9: 22K.Pin_0, J15.pin1
  N10: LED1.anode, 1K.Pin_0
  N11: NPN.B, 22k.Pin_0

notes:
  GND
  OUT
  VCC
  ACK:
  CMD:
  PRG:
  RX RECEIVER
  v0.1 2016
  13
  12
  ~11
  RX<-0
  TX->1
  2
  ~3
  4
  ~5
  ~6
  ~10
  ~9
  8
  7
  AREF
  Rst
  Vin
  A5
  A1
  A0
  A2
  A3
  A4
  5V
  3V3
  SDA
  SCL
  RXShiled, Shield for RX 433 MHz receiver using Attiny85, 0.1
  The RX receiver is powered by the 5V pin and 3V3 pin. The Attiny85 needs 3V3. A voltage divider with 47K and 22K resistors has been introduced to reduce 5V Arduino digital outputs to 3.4V. The reset pin is directly connected to 5V reset pin in Arduino. The RX 5V output is reduced using a 10K resistor and activating pull up resistor in Attiny85 pin.
  .
  1:RST
  RST
  2:A3:3:ON
  3:A2:4:LED
  3:A2:4
  5:PWM:0:ACK
  5:PWM:0
  6:PWM:1:CMD
  7:PWM:2:RX
  by PAKOZM
  Attiny pins
  IOREF
