# Fritzing sketch Remote (saved by Fritzing 0.9.0b)
circuit board: 6.1cm x 3.1cm
breadboards: 1

parts:
  10k = Resistor [tolerance=±5% resistance=10k package=THT]
  MCU = attiny85 [package=dip]
  100nF = Ceramic Capacitor [capacitance=100nF package="100 mil [THT, multilayer]"]
  PINs1 = male pin header, 3 pins [form="♂ (male)"]
  PINs2 = male pin header, 3 pins [form="♂ (male)"]
  1K = Resistor [tolerance=±5% resistance=1k package=THT]
  PRG = Pushbutton [package="[THT]"]
  3V = Battery
  10k_2 = Resistor [tolerance=±5% resistance=10k package=THT]
  LED = LED - 3mm [color="Red (633nm)" package="3 mm [THT]"]
  BTN = Pushbutton [package="[THT]"]
  TX = male pin header, 3 pins [form="♂ (male)"]
  CR2032 = CR2032

nets:
  N1: 10k.Pin_0, MCU.Pin_1, PINs1.pin1, BTN.Pin_3, BTN.Pin_4
  3V: 10k.Pin_1, MCU.Pin_8, 100nF.0, PRG.Pin_1, PRG.Pin_2, 3V.+, TX.pin2, CR2032.+
  N2: MCU.Pin_2, PINs1.pin2, TX.pin3
  N3: MCU.Pin_3, PINs1.pin3, 1K.Pin_0
  GND: MCU.Pin_4, 100nF.1, 3V.-, 10k_2.Pin_1, LED.cathode, BTN.Pin_1, TX.pin1, CR2032.-
  N4: MCU.Pin_5, PINs2.pin1
  N5: MCU.Pin_6, PINs2.pin2
  N6: MCU.Pin_7, PINs2.pin3, PRG.Pin_3, PRG.Pin_4, 10k_2.Pin_0
  N7: 1K.Pin_1, LED.anode

notes:
  3:LED
  5:MOSI
  6:MISO
  2:TX
  1:RST
  Vin
  GND
  7:SCK
  REMOTE V0.3
  PAKOZM (2016)
  -
  Remote, Remote control with 433MHz TX, 0.3
  This circuit fits into a wireless doorbell transmiter.
  CR2032
  7:PRG
  VCC
  data
  +
  .

custom parts:
  CR2032: CR2032 coin cell PCB adapter
